// Logisim project 24.circ as structural Verilog: 1 circuit, main circuit main
module main (
);

  wire clock_1_out, clock_2_out;
  wire [5:0] counter_1_q, counter_2_q;
  wire [6:0] ram_1_data, ram_2_data, shift_register_1_q0, shift_register_1_q1, shift_register_1_q2,
       shift_register_1_q3, shift_register_1_q4, shift_register_1_q5, shift_register_1_q6,
       shift_register_1_q7, shift_register_2_q0, shift_register_2_q1, shift_register_2_q2,
       shift_register_2_q3, shift_register_2_q4, shift_register_2_q5, shift_register_2_q6,
       shift_register_2_q7;

  Counter #(.width(6), .max('h3f)) counter_1 (.Q(counter_1_q), .clk(clock_1_out));  // open: load, D, count, carry, clr
  Clock clock_1 (.out(clock_1_out));
  RAM #(.addrWidth(6), .dataWidth(7)) ram_1 (.addr(counter_1_q), .data(ram_1_data));  // open: sel, clk, ld, clr
  Shift_Register #(.width(7)) shift_register_1 (
    .in(ram_1_data), .clk(clock_1_out), .q0(shift_register_1_q0), .q1(shift_register_1_q1),
    .q2(shift_register_1_q2), .q3(shift_register_1_q3), .q4(shift_register_1_q4), .q5(shift_register_1_q5),
    .q6(shift_register_1_q6), .q7(shift_register_1_q7));  // open: shift, out, load, clr, d0, d1, d2, d3, d4, d5, d6, d7
  DotMatrix #(.matrixcols(8)) dotmatrix_1 (
    .col0(shift_register_1_q0), .col1(shift_register_1_q1), .col2(shift_register_1_q2),
    .col3(shift_register_1_q3), .col4(shift_register_1_q4), .col5(shift_register_1_q5),
    .col6(shift_register_1_q6), .col7(shift_register_1_q7));
  Counter #(.width(6), .max('h3f)) counter_2 (.Q(counter_2_q), .clk(clock_2_out));  // open: load, D, count, carry, clr
  Clock clock_2 (.out(clock_2_out));
  RAM #(.addrWidth(6), .dataWidth(7)) ram_2 (.addr(counter_2_q), .data(ram_2_data));  // open: sel, clk, ld, clr
  Shift_Register #(.width(7)) shift_register_2 (
    .in(ram_2_data), .clk(clock_2_out), .q0(shift_register_2_q0), .q1(shift_register_2_q1),
    .q2(shift_register_2_q2), .q3(shift_register_2_q3), .q4(shift_register_2_q4), .q5(shift_register_2_q5),
    .q6(shift_register_2_q6), .q7(shift_register_2_q7));  // open: shift, out, load, clr, d0, d1, d2, d3, d4, d5, d6, d7
  DotMatrix #(.matrixcols(8)) dotmatrix_2 (
    .col0(shift_register_2_q0), .col1(shift_register_2_q1), .col2(shift_register_2_q2),
    .col3(shift_register_2_q3), .col4(shift_register_2_q4), .col5(shift_register_2_q5),
    .col6(shift_register_2_q6), .col7(shift_register_2_q7));
endmodule
