// Logisim project 29.10.circ as structural Verilog: 2 circuits, main circuit main
module main (
  input  [3:0] in_1,
  output out_2,
  output out_3,
  output out_4,
  output out_5,
  output out_6,
  output out_7,
  output out_8
);

  wire and_1_out, and_2_out, and_3_out, and_4_out, and_5_out, and_6_out, and_7_out, and_8_out, and_9_out,
       and_10_out, and_11_out, and_12_out, or_1_out, or_2_out, xnor_1_out, xnor_2_out;

  and and_1 (and_1_out, ~in_1[2], ~in_1[0]);  // AND_Gate
  and and_2 (and_2_out, in_1[1], ~in_1[0]);  // AND_Gate
  and and_3 (and_3_out, ~in_1[1], ~in_1[0]);  // AND_Gate
  and and_4 (and_4_out, ~in_1[1], in_1[2]);  // AND_Gate
  and and_5 (and_5_out, ~in_1[0], in_1[2]);  // AND_Gate
  and and_6 (and_6_out, ~in_1[1], in_1[2]);  // AND_Gate
  and and_7 (and_7_out, ~in_1[2], in_1[1]);  // AND_Gate
  and and_8 (and_8_out, ~in_1[0], in_1[1]);  // AND_Gate
  or or_1 (or_1_out, in_1[3], in_1[1]);
  xnor xnor_1 (xnor_1_out, in_1[2], in_1[0]);
  xnor xnor_2 (xnor_2_out, in_1[1], in_1[0]);
  or or_2 (or_2_out, in_1[2], ~in_1[1]);  // OR_Gate
  and and_9 (and_9_out, ~in_1[2], ~in_1[0]);  // AND_Gate
  and and_10 (and_10_out, ~in_1[2], in_1[1]);  // AND_Gate
  and and_11 (and_11_out, ~in_1[0], in_1[1]);  // AND_Gate
  and and_12 (and_12_out, ~in_1[1], in_1[0], in_1[2]);  // AND_Gate
  or or_3 (out_6, and_1_out, and_2_out);
  or or_4 (out_2, or_1_out, xnor_1_out);
  or or_5 (out_3, xnor_2_out, ~in_1[2]);  // OR_Gate
  or or_6 (out_4, or_2_out, in_1[0]);
  or or_7 (out_7, in_1[3], and_3_out, and_4_out, and_5_out);
  or or_8 (out_8, in_1[3], and_6_out, and_7_out, and_8_out);
  or or_9 (out_5, in_1[3], and_9_out, and_10_out, and_11_out, and_12_out);
endmodule

module circuito1 (
  input  [3:0] in_1
);

  wire main_1_out_2, main_1_out_3, main_1_out_4, main_1_out_5, main_1_out_6, main_1_out_7, main_1_out_8;

  main main_1 (
    .out_5(main_1_out_5), .out_6(main_1_out_6), .out_7(main_1_out_7), .out_8(main_1_out_8),
    .out_4(main_1_out_4), .out_3(main_1_out_3), .out_2(main_1_out_2), .in_1(in_1));
  _7_Segment_Display u_7_segment_display_1 (
    .g(main_1_out_8), .f(main_1_out_7), .a(main_1_out_2), .b(main_1_out_3), .e(main_1_out_6),
    .d(main_1_out_5), .c(main_1_out_4));  // open: dp
endmodule
