// Logisim project EX 2.circ as structural Verilog: 2 circuits, main circuit main
module add (
  input  [3:0] in_1,
  input  [3:0] in_2,
  input  in_3,
  input  in_4,
  input  in_5,
  output out_6,
  output out_7,
  output out_8
);

  wire main_3_vai_1, main_4_vai_1, main_5_vai_1;
  wire [3:0] main_5_s;

  main main_1 (.s(out_8), .vai_1(out_7), .a(in_3), .b(in_4), .c(in_5));
  main main_2 (.s(main_5_s[3]), .vai_1(out_6), .a(in_2[3]), .b(in_1[3]), .c(main_3_vai_1));
  main main_3 (.s(main_5_s[2]), .vai_1(main_3_vai_1), .a(in_2[2]), .b(in_1[2]), .c(main_4_vai_1));
  // Probe on main_5_s
  main main_4 (.s(main_5_s[1]), .vai_1(main_4_vai_1), .a(in_2[1]), .b(in_1[1]), .c(main_5_vai_1));
  main main_5 (.s(main_5_s[0]), .vai_1(main_5_vai_1), .a(in_2[0]), .b(in_1[0]), .c(1'b0));
endmodule

module main (
  input  a,
  input  b,
  input  c,
  output s,
  output vai_1
);

  wire and_1_out, and_2_out, or_1_out, xor_1_out;

  xor xor_1 (xor_1_out, b, a);
  or or_1 (or_1_out, c, b);
  and and_1 (and_1_out, b, c);
  xor xor_2 (s, c, xor_1_out);
  and and_2 (and_2_out, or_1_out, a);
  or or_2 (vai_1, and_2_out, and_1_out);
endmodule
