// Logisim project dvsdasd.circ as structural Verilog: 1 circuit, main circuit main
module main (
  input  in_1,
  input  in_2,
  input  in_3,
  input  in_4,
  output out_5
);

  wire xor_1_out, xor_2_out;

  xor xor_1 (xor_1_out, in_4, in_3);
  xor xor_2 (xor_2_out, in_2, in_1);
  xor xor_3 (out_5, xor_1_out, xor_2_out);
endmodule
