// Logisim project jurados.circ as structural Verilog: 2 circuits, main circuit main
module main (
  input  [3:0] in_1,
  output out_2
);

  wire and_1_out, and_2_out, and_3_out, and_4_out, and_5_out;

  and and_1 (and_1_out, ~in_1[3], in_1[2], in_1[1], in_1[0]);  // AND_Gate
  and and_2 (and_2_out, in_1[3], ~in_1[2], in_1[1], in_1[0]);  // AND_Gate
  and and_3 (and_3_out, in_1[3], in_1[2], ~in_1[1], in_1[0]);  // AND_Gate
  and and_4 (and_4_out, in_1[3], in_1[2], in_1[1], ~in_1[0]);  // AND_Gate
  and and_5 (and_5_out, in_1[3], in_1[2], in_1[1], in_1[0]);
  or or_1 (out_2, and_1_out, and_2_out, and_3_out, and_4_out, and_5_out);
endmodule

module circuito (
  input  [3:0] in_1
);

  wire main_1_out_2;

  LED led_1 (.in(main_1_out_2));
  main main_1 (.out_2(main_1_out_2), .in_1(in_1));
endmodule
